// Logisim project GG.circ as structural Verilog: 1 circuit, main circuit main
module main (
  input  C,
  input  D,
  input  in_3,
  input  B,
  output out_5
);

  wire and_1_out, and_2_out, and_3_out, and_4_out, nand_1_out, not_1_out, not_2_out, not_3_out, not_4_out,
       undriven, undriven_2, xor_1_out;

  not not_1 (not_1_out, C);
  not not_2 (not_2_out, D);
  not not_3 (not_3_out, undriven);
  nand nand_1 (nand_1_out, C, D);
  xor xor_1 (xor_1_out, not_1_out, D);
  not not_4 (not_4_out, undriven_2);
  and and_1 (and_1_out, not_3_out, nand_1_out, not_4_out);
  and and_2 (and_2_out, undriven, xor_1_out, not_4_out);
  and and_3 (and_3_out, C, undriven_2, not_3_out);
  and and_4 (and_4_out, undriven, undriven_2, not_2_out);
  or or_1 (out_5, and_1_out, and_2_out, and_3_out, and_4_out);

  // Notes on the sheet:
  //   A
  //   (CD)'
  //   AB'(CD+C'D')
  //   A'BC
  //   ABD'
  //   A'B'(CD)'
endmodule
